# Fritzing sketch raspberry-Xiao-bmp280 (saved by Fritzing 0.8.7b)
breadboards: 1

parts:
  J1 = Raspberry Pi Header 40pin [form="♂ (male)" package=THT]
  LED1 = LED - 5mm [color="Red (633nm)" package="5 mm [THT]"]
  M1 = BMP280
  R1 = Resistor [tolerance=±5% resistance=4.7k package=THT]
  R2 = Resistor [tolerance=±5% resistance=4.7k package=THT]
  Mod1 = seeeduino-xiao
  R3 = Resistor [tolerance=±5% resistance=220 package=THT]

nets:
  3V3: J1.3v3, M1.VIN, Mod1.3V3
  N1: J1.GPIO2, M1.SDA
  N2: J1.GPIO3, M1.SCL
  GND: J1.GND, M1.GND, Mod1.GND, R3.Pin_1
  N3: LED1.cathode, R3.Pin_0
  N4: LED1.anode, Mod1.D3
  N5: R1.Pin_0, R2.Pin_0

notes:
  Raspberry PI 4 header
  Remove Xiao 3.3v when Arduino IDE PC is connected to USB-C

custom parts:
  Raspberry Pi Header 40pin: Raspberry Pi 40 pin header - for creating your own shields.
  BMP280: Temperature Humidity Barometric presure Sensor, I2C
  seeeduino-xiao: Seeeduino XIAO processor board.
